# Fritzing sketch doorbell-circuit (common anode) (saved by Fritzing 0.9.3b)
breadboards: 1

parts:
  LED1 = RGB LED (com. cathode, rbg) [package="5 mm [THT]"]
  Raspberry_Pi_1 = Raspberry Pi 3 [part_number=RPI-3-V1.2]
  R1 = Resistor [tolerance=±5% resistance=330 package=THT]
  J1 = Piezo Speaker  # not connected

nets:
  N1: LED1.red_anode, Raspberry_Pi_1.GND
  N2: LED1.common_cathode, R1.Pin_0
  N3: LED1.blue_anode, Raspberry_Pi_1.GIPO27
  N4: LED1.green_anode, Raspberry_Pi_1.GIPO22
