# Fritzing sketch adafruit-servo-board (saved by Fritzing 0.9.3b)

parts:
  Part1 = Adafruit 16-Channel PWM + Servo HAT [part_number="Adafruit #2327"]
  S1 = H-Bridge with L298N
  J1 = Basic Servo
  J2 = Basic Servo
  LED1 = LED - 5mm [color="Green (555nm)" package="5 mm [THT]"]
  LED2 = LED - 5mm [color="Red (633nm)" package="5 mm [THT]"]
  R1 = Resistor [tolerance=±5% resistance=330 package=THT]
  R2 = Resistor [tolerance=±5% resistance=330 package=THT]
  J3 = Piezo Speaker

nets:
  N1: Part1.PWRIN, S1.VCC
  GND: Part1.GND, S1.GND, J1.gnd, J2.gnd, LED1.cathode, LED2.cathode, J3.pin1
  N2: Part1.GPIO27, S1.IN3
  N3: Part1.GPIO22, S1.IN4
  N4: Part1.GPIO5, S1.IN1
  N5: Part1.GPIO6, S1.IN2
  N6: Part1.GPIO12, J3.pin2
  N7: Part1.#1, J1.pulse
  VCC: Part1.+5V, J1.vcc, J2.vcc
  N8: Part1.#0, J2.pulse
  N9: Part1.5.0V, R1.Pin_0, R2.Pin_0

custom parts:
  Adafruit 16-Channel PWM + Servo HAT: The Raspberry Pi is a wonderful little computer, but one thing it isn't very good at is controlling DC Servo Motors - these motors need very specific and repetitive timing pulses to set the position. Instead of asking the Pi Linux kernel to send these signals, pop on this handy HAT! It adds the capability to control 16 Servos with perfect timing. It can also do PWM up to 1.6 KHz with 12 bit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
  H-Bridge with L298N: h-bridge
