# Fritzing sketch l289n-dc-jack (saved by Fritzing 0.9.3b)

parts:
  JACK1 = 2.1mm Barrel Jack with Terminal Block
  S1 = H-Bridge with L298N

nets:
  N1: JACK1.POS, S1.VCC
  N2: JACK1.NEG, S1.GND

custom parts:
  H-Bridge with L298N: h-bridge
