# Fritzing sketch servo-circuit (saved by Fritzing 0.9.3b)
breadboards: 1

parts:
  Raspberry_Pi_1 = Raspberry Pi 3 [part_number=RPI-3-V1.2]
  R1 = Resistor [tolerance=±5% resistance=220 package=THT]
  LED2 = LED - 5mm [color="Red (633nm)" package="5 mm [THT]"]
  J1 = Basic Servo

nets:
  GND: Raspberry_Pi_1.GND, R1.Pin_1, J1.gnd
  N1: Raspberry_Pi_1.GPIO14, LED2.anode
  5V: Raspberry_Pi_1.5V, J1.vcc
