# Fritzing sketch distance-sensor (saved by Fritzing 0.9.3b)
breadboards: 1

parts:
  Raspberry_Pi_1 = Raspberry Pi 3 [part_number=RPI-3-V1.2]
  hc-sr1 = hc-sr04
  R1 = Resistor [tolerance=±5% resistance=330 package=THT]
  R2 = Resistor [tolerance=±5% resistance=470 package=THT]

nets:
  N1: Raspberry_Pi_1.GPIO17, hc-sr1.Trig
  GND: Raspberry_Pi_1.GND, hc-sr1.GND, R2.Pin_1
  N2: Raspberry_Pi_1.GPIO18, R1.Pin_1, R2.Pin_0
  5V: Raspberry_Pi_1.5V, hc-sr1.VCC
  N3: hc-sr1.Echo, R1.Pin_0
