# Fritzing sketch hello-led (saved by Fritzing 0.9.3b)
breadboards: 1

parts:
  Raspberry_Pi_1 = Raspberry Pi 3 [part_number=RPI-3-V1.2]
  hc-sr1 = hc-sr04
  R1 = Resistor [tolerance=±5% resistance=330 package=THT]
  R2 = Resistor [tolerance=±5% resistance=470 package=THT]
  PIR1 = PIR sensor
  LED1 = LED - 3mm [color="Red (633nm)" package="3 mm [THT]"]
  R3 = Resistor [tolerance=±5% resistance=220 package="0805 [SMD]"]

nets:
  N1: Raspberry_Pi_1.GPIO4, PIR1.SIG
  N2: Raspberry_Pi_1.GPIO17, hc-sr1.Trig
  N3: Raspberry_Pi_1.GPIO21, R3.Pin_0
  GND: Raspberry_Pi_1.GND, hc-sr1.GND, R2.Pin_1, PIR1.GND, LED1.cathode
  N4: Raspberry_Pi_1.GPIO18, R1.Pin_1, R2.Pin_0
  5V: Raspberry_Pi_1.5V, hc-sr1.VCC, PIR1.VDD
  N5: hc-sr1.Echo, R1.Pin_0
  N6: LED1.anode, R3.Pin_1
