# Fritzing sketch pir-sensor (saved by Fritzing 0.9.3b)
breadboards: 1

parts:
  Raspberry_Pi_1 = Raspberry Pi 3 [part_number=RPI-3-V1.2]
  PIR1 = PIR_sensor

nets:
  N1: Raspberry_Pi_1.GPIO4, PIR1.connector2
  N2: Raspberry_Pi_1.GND, PIR1.connector3
  N3: Raspberry_Pi_1.5V, PIR1.connector1
