# Fritzing sketch pushbutton-led (saved by Fritzing 0.9.3b)
breadboards: 1

parts:
  Raspberry_Pi_1 = Raspberry Pi 3 [part_number=RPI-3-V1.2]
  S1 = Round Pushbutton
  R1 = Resistor [tolerance=±5% resistance=1k package=THT]
  LED1 = LED - 3mm [color="Red (633nm)" package="3 mm [THT]"]

nets:
  N1: Raspberry_Pi_1.GIPO4, S1.leg1
  N2: Raspberry_Pi_1.GIPO17, R1.Pin_0
  N3: Raspberry_Pi_1.GND, S1.leg0, LED1.cathode
  N4: R1.Pin_1, LED1.anode
